# Fritzing sketch Synthesizer_Fritzing_Diagram (saved by Fritzing 0.9.3b)
breadboards: 5

parts:
  Part1 = PocketBeagle
  S1 = Momentary Switch [package=ksa_sealed_tac_switch]
  S2 = Momentary Switch [package=ksa_sealed_tac_switch]
  S3 = Momentary Switch [package=ksa_sealed_tac_switch]
  S4 = Momentary Switch [package=ksa_sealed_tac_switch]
  S5 = Momentary Switch [package=ksa_sealed_tac_switch]
  S6 = Momentary Switch [package=ksa_sealed_tac_switch]
  S7 = Momentary Switch [package=ksa_sealed_tac_switch]
  S8 = Momentary Switch [package=ksa_sealed_tac_switch]
  S9 = Momentary Switch [package=ksa_sealed_tac_switch]
  S10 = Momentary Switch [package=ksa_sealed_tac_switch]
  S11 = Momentary Switch [package=ksa_sealed_tac_switch]
  S12 = Momentary Switch [package=ksa_sealed_tac_switch]
  R1 = Resistor [tolerance=±5% resistance=10k package="0603 [SMD]"]
  R2 = Resistor [tolerance=±5% resistance=10k package="0603 [SMD]"]
  R3 = Resistor [tolerance=±5% resistance=10k package="0603 [SMD]"]
  R4 = Resistor [tolerance=±5% resistance=10k package="0603 [SMD]"]
  R5 = Resistor [tolerance=±5% resistance=10k package="0603 [SMD]"]
  R6 = Resistor [tolerance=±5% resistance=10k package="0603 [SMD]"]
  R7 = Resistor [tolerance=±5% resistance=10k package="0603 [SMD]"]
  U1 = SWITCH_SPDT [package=kps-1290]
  R8 = Resistor [tolerance=±5% resistance=10k package="0603 [SMD]"]
  U2 = POT [package=pot_alpha_rv16af-20]
  U3 = POT [package=pot_alpha_rv16af-20]
  U4 = SWITCH_SPDT [package=kps-1290]
  U5 = POT [package=pot_alpha_rv16af-20]
  J1 = Piezo Speaker
  J2 = Piezo Speaker
  J3 = Piezo Speaker
  U6 = POT [package=pot_alpha_rv16af-20]
  U8 = POT [package=pot_alpha_rv16af-20]

nets:
  N1: Part1.GPIO89, S10.1
  N2: Part1.GND, J2.pin1, J2.pin2, J3.pin1, J3.pin2, U6.A, U8.A
  N3: Part1.AIN.VREFN, U2.A, U3.A
  N4: Part1.AIN.VREFP, U2.E, U3.E
  N5: Part1.AIN0(1.8V), U3.S
  N6: Part1.GPIO20, S2.1
  N7: Part1.AIN1(1.8V), U2.S
  N8: Part1.GPIO26, S11.1
  N9: Part1.PWM0A, U4.P
  N10: Part1.PWM1A, U6.S
  N11: Part1.GPIO23, U8.S
  N12: Part1.GPIO58, S8.1
  N13: Part1.GPIO60, S7.1
  N14: Part1.GPIO65, S6.1
  N15: Part1.GPIO47, S3.1
  N16: S1.3, S10.4, R1.Pin_0
  N17: S2.3, S11.4, R2.Pin_0
  N18: S3.4, S6.3, R6.Pin_0
  N19: S4.4, S7.3, R5.Pin_0
  N20: S5.3, R7.Pin_0
  N21: S8.3, S12.4, R4.Pin_0
  N22: S9.3, R3.Pin_0
  N23: R1.Pin_1, R2.Pin_1, R3.Pin_1, R4.Pin_1, R5.Pin_1, R6.Pin_1, R7.Pin_1, R8.Pin_1, U5.A, J1.pin1, J1.pin2
  N24: U1.S, R8.Pin_0
  N25: U4.S, U5.S
